// Logisim project arbitro.circ as structural Verilog: 6 circuits, main circuit arbitro corregido 
module arbitro_incorrecto (
  input  Rq1,
  input  Rq2,
  output ack1,
  output ack2
);

  wire clock_1_out, clock_2_out, d0_1_d0, D0_Q0_q, d1_1_d1, D1_Q1_q;

  // Probe on D0_Q0_q
  // Probe on D1_Q1_q
  Ack1 ack1_1 (.q0(D0_Q0_q), .q1(D1_Q1_q), .Rq1(Rq1), .Rq2(Rq2), .ack1(ack1));
  Ack2 ack2_1 (.q0(D0_Q0_q), .q1(D1_Q1_q), .Rq1(Rq1), .Rq2(Rq2), .ack2(ack2));
  D0 d0_1 (.q0(D0_Q0_q), .q1(D1_Q1_q), .Rq1(Rq1), .Rq2(Rq2), .d0(d0_1_d0));
  D1 d1_1 (.q0(D0_Q0_q), .q1(Rq2), .Rq1(Rq1), .Rq2(Rq2), .d1(d1_1_d1));
  Register #(.width(1), .trigger("falling")) D0_Q0 (.D(d0_1_d0), .Q(D0_Q0_q), .clk(clock_1_out));  // open: en, clr
  Clock clock_1 (.out(clock_1_out));
  Register #(.width(1), .trigger("falling")) D1_Q1 (.D(d1_1_d1), .Q(D1_Q1_q), .clk(clock_2_out));  // open: en, clr
  Clock clock_2 (.out(clock_2_out));
endmodule

module D0 (
  input  q0,
  input  q1,
  input  Rq1,
  input  Rq2,
  output d0
);

  wire and_1_out, and_2_out, not_1_out;

  not not_1 (not_1_out, Rq1);
  and and_1 (and_1_out, q0, Rq2);
  and and_2 (and_2_out, not_1_out, Rq2);
  or or_1 (d0, and_1_out, and_2_out);

  // Notes on the sheet:
  //   ~Rq1Rq2 + Q0 Q1 + Q0 Rq2
endmodule

module D1 (
  input  q0,
  input  q1,
  input  Rq1,
  input  Rq2,
  output d1
);

  wire and_1_out, and_2_out, not_1_out, not_2_out;

  not not_1 (not_1_out, q0);
  not not_2 (not_2_out, Rq2);
  and and_1 (and_1_out, not_1_out, Rq1);
  and and_2 (and_2_out, Rq1, not_2_out);
  or or_1 (d1, and_1_out, and_2_out);

  // Notes on the sheet:
  //   Rq1~Rq2 + ~Q0Rq1
endmodule

module Ack1 (
  input  q0,
  input  q1,
  input  Rq1,
  input  Rq2,
  output ack1
);

  wire and_1_out, and_2_out, not_1_out, not_2_out;

  not not_1 (not_1_out, q0);
  not not_2 (not_2_out, Rq2);
  and and_1 (and_1_out, not_1_out, Rq1);
  and and_2 (and_2_out, Rq1, not_2_out);
  or or_1 (ack1, and_1_out, and_2_out);

  // Notes on the sheet:
  //   Rq1~Rq2 + ~Q0Rq1
endmodule

module Ack2 (
  input  q0,
  input  q1,
  input  Rq1,
  input  Rq2,
  output ack2
);

  wire and_1_out, and_2_out, not_1_out;

  not not_1 (not_1_out, Rq1);
  and and_1 (and_1_out, q0, Rq2);
  and and_2 (and_2_out, not_1_out, Rq2);
  or or_1 (ack2, and_1_out, and_2_out);
endmodule

module arbitro_corregido (
  input  Rq1,
  input  Rq2,
  output ack1,
  output ack2
);

  wire clock_1_out, clock_2_out, d0_1_d0, d1_1_d1;

  // Probe on ack1
  // Probe on ack2
  D0 d0_1 (.q0(ack1), .q1(ack2), .Rq1(Rq1), .Rq2(Rq2), .d0(d0_1_d0));
  D1 d1_1 (.q0(ack1), .q1(Rq2), .Rq1(Rq1), .Rq2(Rq2), .d1(d1_1_d1));
  Register #(.width(1), .trigger("falling")) D0_Q0 (.D(d0_1_d0), .Q(ack1), .clk(clock_1_out));  // open: en, clr
  Clock clock_1 (.out(clock_1_out));
  Register #(.width(1), .trigger("falling")) D1_Q1 (.D(d1_1_d1), .Q(ack2), .clk(clock_2_out));  // open: en, clr
  Clock clock_2 (.out(clock_2_out));
endmodule
