// Logisim project muxcon.circ as structural Verilog: 6 circuits, main circuit OUT
module OUT (
  input  Q1,
  input  IN0,
  input  IN1,
  input  IN2,
  input  S1,
  input  S0,
  input  Q0,
  output OUT
);

  wire and_1_out, and_2_out, and_3_out, and_4_out, and_5_out, and_6_out, and_7_out, and_8_out, and_9_out,
       and_10_out, not_1_out, not_2_out, not_3_out, not_4_out, or_1_out, or_2_out;

  not not_1 (not_1_out, S1);
  not not_2 (not_2_out, S0);
  not not_3 (not_3_out, Q1);
  and and_1 (and_1_out, not_1_out, not_2_out, IN0);
  and and_2 (and_2_out, not_1_out, S0, IN1);
  and and_3 (and_3_out, S1, S0, IN0, not_3_out);
  and and_4 (and_4_out, S1, not_2_out, IN2);
  and and_5 (and_5_out, S0, IN1, Q1);
  and and_6 (and_6_out, not_1_out, not_2_out, IN0);
  and and_7 (and_7_out, not_1_out, S0, IN1);
  and and_8 (and_8_out, S1, IN2);
  or or_1 (or_1_out, and_1_out, and_2_out, and_3_out, and_4_out, and_5_out);
  or or_2 (or_2_out, and_6_out, and_7_out, and_8_out);
  not not_4 (not_4_out, Q0);
  and and_9 (and_9_out, not_4_out, or_1_out);
  and and_10 (and_10_out, Q0, or_2_out);
  or or_3 (OUT, and_9_out, and_10_out);

  // Notes on the sheet:
  //   OUT = ~Q0 * (~S1*~S0*IN0 + ~S1*S0*IN1 + S1*S0*IN0 + S1*~S0*IN2 + S0*IN1*Q1) + Q0 * (~S1*~S0*IN0 + ~S1*S0*IN1 + S1*IN2) 
endmodule

module Cond_Mul (
  input  IN0,
  input  IN1,
  input  IN2,
  input  S1,
  input  S0,
  output out_6
);

  wire clock_1_out, clock_2_out, d0_1_d0, d1_1_d1, register_1_q, register_2_q;

  // Probe on register_2_q
  // Probe on register_1_q
  OUT out_1 (.Q1(register_1_q), .Q0(register_2_q), .IN0(IN0), .IN1(IN1), .IN2(IN2), .S1(S1), .S0(S0), .OUT(out_6));
  D1 d1_1 (.Q1(register_1_q), .Q0(register_2_q), .IN0(IN0), .IN1(IN1), .IN2(IN2), .S1(S1), .S0(S0), .D1(d1_1_d1));
  D0 d0_1 (.Q1(register_1_q), .Q0(register_2_q), .IN0(IN0), .IN1(IN1), .IN2(IN2), .S1(S1), .S0(S0), .D0(d0_1_d0));
  Clock clock_1 (.out(clock_1_out));
  Register #(.width(1), .trigger("falling")) register_1 (
    .D(d1_1_d1), .Q(register_1_q), .clk(clock_2_out));  // open: en, clr
  Clock clock_2 (.out(clock_2_out));
  Register #(.width(1), .trigger("falling")) register_2 (
    .D(d0_1_d0), .Q(register_2_q), .clk(clock_1_out));  // open: en, clr
endmodule

module D0 (
  input  Q1,
  input  Q0,
  input  IN0,
  input  IN1,
  input  IN2,
  input  S1,
  input  S0,
  output D0
);

  wire not_1_out;

  not not_1 (not_1_out, Q0);
  and and_1 (D0, Q1, not_1_out, S0, S1);
endmodule

module D1 (
  input  Q1,
  input  Q0,
  input  IN0,
  input  IN1,
  input  IN2,
  input  S1,
  input  S0,
  output D1
);

  wire not_1_out, not_2_out;

  not not_1 (not_1_out, Q1);
  not not_2 (not_2_out, Q0);
  and and_1 (D1, not_1_out, not_2_out, S0, S1);
endmodule

module out_v2 (
  input  Q0,
  input  IN0,
  input  IN1,
  input  IN2,
  input  S1,
  input  S0,
  input  Q1,
  output OUT
);

  wire and_1_out, and_2_out, and_3_out, and_4_out, and_5_out, and_6_out, and_7_out, and_8_out, not_1_out,
       not_2_out, not_3_out, not_4_out, or_1_out, or_2_out;

  not not_1 (not_1_out, S0);
  not not_2 (not_2_out, S1);
  not not_3 (not_3_out, Q0);
  and and_1 (and_1_out, not_2_out, not_1_out, IN0);
  and and_2 (and_2_out, not_2_out, S0, IN1);
  and and_3 (and_3_out, S1, S0, IN0, not_3_out);
  and and_4 (and_4_out, S1, not_1_out, IN2);
  and and_5 (and_5_out, S0, IN1, Q0);
  and and_6 (and_6_out, S1, IN2);
  or or_1 (or_1_out, and_1_out, and_2_out);
  or or_2 (or_2_out, and_3_out, and_4_out, and_5_out);
  not not_4 (not_4_out, Q1);
  and and_7 (and_7_out, or_2_out, not_4_out);
  and and_8 (and_8_out, Q1, and_6_out);
  or or_3 (OUT, or_1_out, and_7_out, and_8_out);

  // Notes on the sheet:
  //   OUT = ~Q0 * ( S1*S0*IN0*~Q1 + S1*~S0*IN + S0*IN1*Q1) + Q0*S1*IN2 + (~S1*~S0*IN1 + ~S1*S0*IN1)
endmodule

module d0_v2 (
  input  Q1,
  input  Q0,
  input  IN0,
  input  IN1,
  input  IN2,
  input  S1,
  input  S0,
  output D0
);

  and and_1 (D0, Q1, S0, S1);
endmodule
