// Logisim project pauta_aux4.circ as structural Verilog
module FIB (
  input  RESET,
  output [7:0] out_2
);

  wire clock_1_out;
  wire [7:0] adder_1_out, multiplexer_1_out, multiplexer_2_out, register_1_q;

  Adder adder_1 (.a(out_2), .b(register_1_q), .out(adder_1_out));  // open: cin, cout
  // Probe on multiplexer_1_out
  Multiplexer #(.width(8)) multiplexer_1 (
    .in0(adder_1_out), .in1(8'h1), .out(multiplexer_1_out), .sel(RESET));  // open: en
  Clock clock_1 (.out(clock_1_out));
  // Probe on register_1_q
  Register #(.trigger("falling")) register_1 (
    .D(multiplexer_1_out), .Q(register_1_q), .clk(clock_1_out));  // open: en, clr
  // Probe on multiplexer_2_out
  Multiplexer #(.width(8)) multiplexer_2 (
    .in0(register_1_q), .in1(8'h1), .out(multiplexer_2_out), .sel(RESET));  // open: en
  Register #(.trigger("falling")) register_2 (.D(multiplexer_2_out), .Q(out_2), .clk(clock_1_out));  // open: en, clr
  // Probe on out_2
endmodule

module SEARCH (
  input  EQ,
  input  GT,
  input  START,
  output [7:0] out_4
);

  wire clock_1_out, clock_2_out;
  wire [7:0] adder_1_out, multiplexer_1_out, multiplexer_2_out, multiplexer_3_out, multiplexer_4_out,
       register_1_q, shifter_1_out, subtractor_1_out;

  Multiplexer #(.width(8), .enable("false")) multiplexer_1 (
    .in0(shifter_1_out), .in1(8'h80), .out(multiplexer_1_out), .sel(START));
  Subtractor subtractor_1 (.a(out_4), .b(shifter_1_out), .out(subtractor_1_out));  // open: bin, bout
  Adder adder_1 (.a(out_4), .b(shifter_1_out), .out(adder_1_out));  // open: cin, cout
  Register #(.trigger("falling")) register_1 (
    .D(multiplexer_1_out), .Q(register_1_q), .clk(clock_1_out));  // open: en, clr
  Clock clock_1 (.out(clock_1_out));
  // Probe on subtractor_1_out
  // Probe on adder_1_out
  Multiplexer #(.width(8), .enable("false")) multiplexer_2 (
    .in0(subtractor_1_out), .in1(adder_1_out), .out(multiplexer_2_out), .sel(GT));
  Shifter #(.shift("lr")) shifter_1 (.in(register_1_q), .\dist (3'b001), .out(shifter_1_out));
  // Probe on multiplexer_3_out
  Multiplexer #(.width(8), .enable("false")) multiplexer_3 (
    .in0(multiplexer_2_out), .in1(out_4), .out(multiplexer_3_out), .sel(EQ));
  // Probe on shifter_1_out
  Multiplexer #(.width(8)) multiplexer_4 (
    .in0(multiplexer_3_out), .in1(8'h80), .out(multiplexer_4_out), .sel(START));  // open: en
  Clock clock_2 (.out(clock_2_out));
  Register #(.trigger("falling")) register_2 (.D(multiplexer_4_out), .Q(out_4), .clk(clock_2_out));  // open: en, clr
  // Probe on out_4
endmodule
