// Logisim project x2y2.circ as structural Verilog: 5 circuits, main circuit main
module main (
  input  [15:0] X,
  input  [15:0] Y,
  input  START,
  output [31:0] Z,
  output RDY
);

  wire clock_1_out, ctrl_1_msel, ctrl_1_mstart, ctrl_1_x2, multiplicador_serial_1_rdy;
  wire [15:0] multiplexer_1_out, RY_q;
  wire [31:0] multiplexer_2_out, multiplexer_3_out, multiplicador_serial_1_out_6, RX2_q;

  Clock clock_1 (.out(clock_1_out));
  Register #(.width(16), .trigger("falling")) RY (.D(Y), .Q(RY_q), .clk(clock_1_out));  // open: en, clr
  Multiplexer #(.width(16), .enable("false")) multiplexer_1 (
    .in0(X), .in1(RY_q), .out(multiplexer_1_out), .sel(ctrl_1_msel));
  CTRL ctrl_1 (
    .START(START), .MULRDY(multiplicador_serial_1_rdy), .CLK(clock_1_out), .READY(RDY),
    .MSTART(ctrl_1_mstart), .MSEL(ctrl_1_msel), .X2(ctrl_1_x2));
  // Probe on multiplicador_serial_1_out_6
  multiplicador_serial multiplicador_serial_1 (
    .Y(multiplexer_1_out), .X(multiplexer_1_out), .START(ctrl_1_mstart), .clk(clock_1_out),
    .RDY(multiplicador_serial_1_rdy), .out_6(multiplicador_serial_1_out_6));
  Adder #(.width(32)) adder_1 (.a(multiplicador_serial_1_out_6), .b(RX2_q), .out(Z));  // open: cin, cout
  Multiplexer #(.width(32), .enable("false")) multiplexer_2 (
    .in0(RX2_q), .in1(multiplicador_serial_1_out_6), .out(multiplexer_2_out), .sel(ctrl_1_x2));
  Multiplexer #(.width(32), .enable("false")) multiplexer_3 (
    .in0(multiplexer_2_out), .in1({32{1'b0}}), .out(multiplexer_3_out), .sel(START));
  // Probe on Z
  Register #(.width(32), .trigger("falling")) RX2 (
    .D(multiplexer_3_out), .Q(RX2_q), .clk(clock_1_out));  // open: en, clr
endmodule

module multiplicador_serial (
  input  [15:0] Y,
  input  [15:0] X,
  input  START,
  input  clk,
  output RDY,
  output [31:0] out_6
);

  wire [15:0] multiplexer_1_out, RX_q, shifter_1_out;
  wire [31:0] adder_1_out, bit_extender_1_out, multiplexer_2_out, multiplexer_3_out, multiplexer_4_out, RY_q,
       shifter_2_out;

  Shifter #(.width(16), .shift("lr")) shifter_1 (.in(RX_q), .\dist (4'b0001), .out(shifter_1_out));
  assign bit_extender_1_out = {{16{1'b0}}, X};  // Bit_Extender bit_extender_1
  Shifter #(.width(32)) shifter_2 (.in(RY_q), .\dist (5'b00001), .out(shifter_2_out));
  Multiplexer #(.width(16), .enable("false")) multiplexer_1 (
    .in0(shifter_1_out), .in1(Y), .out(multiplexer_1_out), .sel(START));
  Multiplexer #(.width(32), .enable("false")) multiplexer_2 (
    .in0(shifter_2_out), .in1(bit_extender_1_out), .out(multiplexer_2_out), .sel(START));
  Register #(.width(32), .trigger("falling")) RY (.D(multiplexer_2_out), .Q(RY_q), .clk(clk));  // open: en, clr
  Multiplexer #(.width(32), .enable("false")) multiplexer_3 (
    .in0(adder_1_out), .in1({32{1'b0}}), .out(multiplexer_3_out), .sel(START));
  Register #(.width(16), .trigger("falling")) RX (.D(multiplexer_1_out), .Q(RX_q), .clk(clk));  // open: en, clr
  Register #(.width(32), .trigger("falling")) RZ (.D(multiplexer_3_out), .Q(out_6), .clk(clk));  // open: en, clr
  NOR16 nor16_1 (.X(RX_q), .O(RDY));
  Multiplexer #(.width(32), .enable("false")) multiplexer_4 (
    .in0({32{1'b0}}), .in1(RY_q), .out(multiplexer_4_out), .sel(RX_q[0]));
  Adder #(.width(32)) adder_1 (.a(multiplexer_4_out), .b(out_6), .out(adder_1_out));  // open: cin, cout
  // Probe on out_6
endmodule

module NOR16 (
  input  [15:0] X,
  output O
);

  nor nor_1 (O, X[7], X[0], X[1], X[2], X[3], X[4], X[5], X[6], X[8], X[9], X[10], X[11], X[12], X[13], X[14], X[15]);
endmodule

module CTRL_COMB (
  input  Q0,
  input  START,
  input  MULRDY,
  output D0,
  output RDY,
  output MSTART,
  output MSEL,
  output X2
);

  wire and_1_out, and_2_out, and_4_out, not_1_out, not_2_out, not_3_out, not_4_out;

  not not_1 (not_1_out, START);
  not not_2 (not_2_out, START);
  not not_3 (not_3_out, START);
  not not_4 (not_4_out, Q0);
  not not_5 (MSEL, START);
  not not_6 (X2, Q0);
  and and_1 (and_1_out, not_1_out, MULRDY);
  and and_2 (and_2_out, Q0, not_2_out);
  and and_3 (RDY, Q0, not_3_out, MULRDY);
  and and_4 (and_4_out, not_4_out, MULRDY);
  or or_1 (D0, and_1_out, and_2_out);
  or or_2 (MSTART, and_4_out, START);
endmodule

module CTRL (
  input  CLK,
  input  START,
  input  MULRDY,
  output READY,
  output MSTART,
  output MSEL,
  output X2
);

  wire ctrl_comb_1_d0, d_ff_1_q;

  D_Flip_Flop #(.trigger("falling")) d_ff_1 (
    .clk(CLK), .D(ctrl_comb_1_d0), .Q(d_ff_1_q));  // open: Qn, preset, en, reset
  CTRL_COMB ctrl_comb_1 (
    .Q0(d_ff_1_q), .START(START), .MULRDY(MULRDY), .D0(ctrl_comb_1_d0), .RDY(READY), .MSTART(MSTART),
    .MSEL(MSEL), .X2(X2));
endmodule
