// Logisim project Circuito_tarea1.circ as structural Verilog: 2 circuits, main circuit main
module main (
  input  START,
  input  X,
  output m1,
  output m0
);

  wire Circuito_Comb_d0, Circuito_Comb_d1, CLK_out, d_ff_1_q, d_ff_2_q;

  Clock CLK (.out(CLK_out));
  D_Flip_Flop #(.trigger("falling")) d_ff_1 (
    .clk(CLK_out), .D(Circuito_Comb_d1), .Q(d_ff_1_q));  // open: Qn, preset, en, reset
  D_Flip_Flop #(.trigger("falling")) d_ff_2 (
    .clk(CLK_out), .D(Circuito_Comb_d0), .Q(d_ff_2_q));  // open: Qn, preset, en, reset
  comb Circuito_Comb (
    .D1(Circuito_Comb_d1), .D0(Circuito_Comb_d0), .q1(d_ff_1_q), .q0(d_ff_2_q), .start(START), .x(X),
    .M1(m0), .M0(m1));
endmodule

module comb (
  input  q1,
  input  q0,
  input  start,
  input  x,
  output D1,
  output D0,
  output M1,
  output M0
);

  wire and_1_out, and_2_out, and_3_out, and_4_out, not_1_out, not_2_out, not_3_out, not_4_out;

  not not_1 (not_1_out, q1);
  not not_2 (not_2_out, start);
  not not_3 (not_3_out, q0);
  not not_4 (not_4_out, x);
  and and_1 (and_1_out, not_2_out, x, not_1_out, not_3_out);
  and and_2 (and_2_out, not_2_out, not_4_out, q0);
  and and_3 (and_3_out, not_4_out, not_2_out, q1);
  and and_4 (and_4_out, x, q0, not_2_out);
  and and_5 (M1, q0, not_2_out);
  and and_6 (M0, q1, not_2_out);
  or or_1 (D0, and_1_out, and_2_out);
  or or_2 (D1, and_3_out, and_4_out);

  // Notes on the sheet:
  //   D1 = q1 -start -x + q0 -start x
  //   D0 = -q1 -q0 -start x  +  q0 -start -x
  //   M1 = q0 -start
  //   M0 = q1 -start
endmodule
