// Logisim project Circuito_tarea2.circ as structural Verilog: 3 circuits, main circuit main
module main (
  input  START,
  input  [9:0] in_2,
  input  [9:0] mantisa,
  input  [5:0] exp,
  input  [5:0] in_5,
  input  CLK,
  output [9:0] mantisa_exit,
  output [5:0] exo_exit,
  output RDY
);

  wire [5:0] norm_first_1_exo_exit;
  wire [9:0] norm_first_1_mantisa_exit;

  norm_first norm_first_1 (
    .START(START), .mantisa(mantisa), .exp(exp), .CLK(CLK), .mantisa_exit(norm_first_1_mantisa_exit),
    .exo_exit(norm_first_1_exo_exit), .RDY(RDY));
  Multiplexer #(.width(10), .enable("false")) multiplexer_1 (
    .in0(in_2), .in1(norm_first_1_mantisa_exit), .out(mantisa_exit), .sel(RDY));
  Multiplexer #(.width(6), .enable("false")) multiplexer_2 (
    .in0(in_5), .in1(norm_first_1_exo_exit), .out(exo_exit), .sel(RDY));
endmodule

module first_bit (
  input  [9:0] X,
  output result
);


  assign result = X[9];
endmodule

module norm_first (
  input  START,
  input  [9:0] mantisa,
  input  [5:0] exp,
  input  CLK,
  output [9:0] mantisa_exit,
  output [5:0] exo_exit,
  output RDY
);

  wire [5:0] multiplexer_2_out, subtractor_1_out;
  wire [9:0] multiplexer_1_out, shifter_1_out;

  Shifter #(.width(10)) shifter_1 (.in(mantisa_exit), .\dist (4'b0001), .out(shifter_1_out));
  Multiplexer #(.width(10), .enable("false")) multiplexer_1 (
    .in0(shifter_1_out), .in1(mantisa), .out(multiplexer_1_out), .sel(START));
  Subtractor #(.width(6)) subtractor_1 (.a(exo_exit), .b(6'b000001), .out(subtractor_1_out));  // open: bin, bout
  Multiplexer #(.width(6), .enable("false")) multiplexer_2 (
    .in0(subtractor_1_out), .in1(exp), .out(multiplexer_2_out), .sel(START));
  Register #(.width(10), .trigger("falling")) register_1 (
    .D(multiplexer_1_out), .Q(mantisa_exit), .clk(CLK));  // open: en, clr
  Register #(.width(6), .trigger("falling")) register_2 (
    .D(multiplexer_2_out), .Q(exo_exit), .clk(CLK));  // open: en, clr
  first_bit first_bit_1 (.X(mantisa_exit), .result(RDY));
endmodule
